# Fritzing sketch circuit (saved by Fritzing 0.9.10b)
breadboards: 1

parts:
  Part1 = Arduino Nano (Rev3.0)
  R1 = Basic Flex Resistor
  R2 = Basic Flex Resistor
  R3 = Basic Flex Resistor
  R4 = Basic Flex Resistor
  Grove1 = Grove 3 Axis Digital Accelerometer 16g
  R5 = Resistor [tolerance=±5% resistance=10k package="0402 [SMD]"]  # not connected
  R6 = Resistor [tolerance=±5% resistance=10k package="0402 [SMD]"]  # not connected
  R7 = Resistor [tolerance=±5% resistance=10k package="0402 [SMD]"]
  R8 = Resistor [tolerance=±5% resistance=10k package="0402 [SMD]"]  # not connected

nets:
  GND: Part1.D0/RX, Part1.RESET, Part1.GND, R1.pin_1, R2.pin_1, R3.pin_1, R4.pin_1, Grove1.GND
  N1: Part1.D11/MOSI, Part1.A0
  N2: Part1.5V, R7.Pin_0
